// Logisim project Circuito 2.circ as structural Verilog: 1 circuit, main circuit main
module main (
  input  in_1,
  input  in_2,
  input  in_3,
  input  in_4,
  input  in_5,
  input  in_6,
  input  in_7,
  input  in_8,
  input  in_9
);

  wire and_1_out, nand_1_out, nor_1_out, not_1_out, or_1_out;

  and and_1 (and_1_out, in_1, in_2);
  or or_1 (or_1_out, in_3, in_4);
  not not_1 (not_1_out, in_9);
  LED led_1 (.in(and_1_out));
  LED led_2 (.in(or_1_out));
  nand nand_1 (nand_1_out, in_5, in_6);
  LED led_3 (.in(nand_1_out));
  nor nor_1 (nor_1_out, in_7, in_8);
  LED led_4 (.in(nor_1_out));
  LED led_5 (.in(not_1_out));
endmodule
