// Logisim project Circuito 3.circ as structural Verilog: 1 circuit, main circuit main
module main (
  input  in_1
);

  wire and_1_out, and_2_out, and_3_out, nand_1_out, nor_1_out, not_1_out, not_2_out, not_3_out, not_4_out,
       not_5_out, not_6_out, not_7_out, not_8_out, not_9_out, not_10_out, not_11_out, or_1_out, or_2_out,
       or_3_out;
  wire [1:0] counter_1_q;

  Counter #(.width(2), .max('h3)) counter_1 (.Q(counter_1_q), .clk(in_1));  // open: load, D, count, carry, clr
  not not_1 (not_1_out, counter_1_q[0]);
  not not_2 (not_2_out, counter_1_q[1]);
  not not_3 (not_3_out, counter_1_q[0]);
  not not_4 (not_4_out, counter_1_q[1]);
  nand nand_1 (nand_1_out, counter_1_q[0], counter_1_q[1]);
  or or_1 (or_1_out, not_1_out, not_2_out);
  nor nor_1 (nor_1_out, counter_1_q[0], counter_1_q[1]);
  and and_1 (and_1_out, not_3_out, not_4_out);
  not not_5 (not_5_out, counter_1_q[0]);
  LED led_1 (.in(nand_1_out));
  LED led_2 (.in(or_1_out));
  LED led_3 (.in(nor_1_out));
  LED led_4 (.in(and_1_out));
  LED led_5 (.in(not_5_out));
  not not_6 (not_6_out, counter_1_q[0]);
  not not_7 (not_7_out, counter_1_q[1]);
  not not_8 (not_8_out, counter_1_q[0]);
  not not_9 (not_9_out, counter_1_q[1]);
  and and_2 (and_2_out, counter_1_q[0], counter_1_q[1]);
  or or_2 (or_2_out, not_6_out, not_7_out);
  or or_3 (or_3_out, counter_1_q[0], counter_1_q[1]);
  and and_3 (and_3_out, not_8_out, not_9_out);
  LED led_6 (.in(and_2_out));
  not not_10 (not_10_out, or_2_out);
  LED led_7 (.in(not_10_out));
  LED led_8 (.in(or_3_out));
  LED led_9 (.in(not_11_out));
  not not_11 (not_11_out, and_3_out);
endmodule
