// Logisim project circuito.circ as structural Verilog: 1 circuit, main circuit main
module main (
  input  D1,
  input  C1,
  input  B1,
  input  A1,
  input  D0,
  input  C0,
  input  B0,
  input  A0,
  output b6,
  output b5,
  output b4,
  output b3,
  output b2,
  output b1_2,
  output b0_2
);

  wire n7483_1_p1, n7483_1_p4, n7483_1_p9;

  // _7483 7483_1: pin names not known; wires that end beside it: n7483_1_p1, b3, D1, n7483_1_p4, b4, C1, C1, 1'b0, n7483_1_p9, b5, b6, D1, 1'b0
  // _7483 7483_2: pin names not known; wires that end beside it: C0, b1_2, B1, B0, b2, A1, A1, 1'b0, D0, n7483_1_p9, n7483_1_p4, n7483_1_p1, B1, 1'b0

  assign b0_2 = A0;
endmodule
