// Logisim project jokepo.circ as structural Verilog: 4 circuits, main circuit contaDe1A7
module main (
);

  wire and_1_out, button_1_out, button_2_out, button_3_out, button_4_out, button_5_out, button_6_out,
       button_7_out, clock_1_out, contagem_1_out_5, or_1_out;
  wire [1:0] jogo_1_out_9;
  wire [6:0] contagem_1_out_4, multiplexer_1_out, rom_1_data;

  Multiplexer #(.select(2), .width(7)) multiplexer_1 (
    .in1({7{1'b0}}), .in2(7'b0010000), .in3(7'b0100000), .out(multiplexer_1_out), .sel(jogo_1_out_9),
    .en(1'b1));  // open: in0
  Button button_1 (.out(button_1_out));
  and and_1 (and_1_out, or_1_out, clock_1_out, ~contagem_1_out_5);  // AND_Gate
  or or_1 (or_1_out, jogo_1_out_9[1], jogo_1_out_9[0]);
  Clock clock_1 (.out(clock_1_out));
  Button button_2 (.out(button_2_out));
  Button button_3 (.out(button_3_out));
  jogo jogo_1 (
    .in_1(button_1_out), .in_2(button_2_out), .in_3(button_3_out), .in_4(button_4_out), .in_5(button_5_out),
    .in_6(button_6_out), .in_7(button_7_out), .out_8(jogo_1_out_9[1]), .out_9(jogo_1_out_9[0]));
  Button button_4 (.out(button_4_out));
  Button button_5 (.out(button_5_out));
  contagem contagem_1 (
    .in_1(multiplexer_1_out), .in_3(and_1_out), .in_2(button_7_out), .out_4(contagem_1_out_4),
    .out_5(contagem_1_out_5));
  Button button_6 (.out(button_6_out));
  Button button_7 (.out(button_7_out));
  ROM #(.addrWidth(7), .dataWidth(7)) rom_1 (.addr(contagem_1_out_4), .data(rom_1_data));  // open: sel
  TTY tty_1 (.data(rom_1_data), .clk(and_1_out), .clr(button_7_out));  // open: we

  // Notes on the sheet:
  //       Pedra                  Papel               Tesoura
  //       Pedra                  Papel               Tesoura
  //   Reiniciar
  //   contents of rom_1 (hex, n*v repeats v):
  //   6a 6f 67 61 64 6f 72 20 31 20 76 65 6e 63 65 75 6a 6f 67 61 64 6f 72 20 32 20 76 65 6e 63 65 75 64
  //   65 75 20 65 6d 70 61 74 65 6*21
endmodule

module contaDe1A7 (
  input  in_1,
  input  in_2,
  output out_3
);

  wire and_1_out, not_1_out;
  wire [4:0] counter_1_q;

  and and_1 (and_1_out, in_2, not_1_out);
  Counter #(.width(5), .max('h1f)) counter_1 (
    .Q(counter_1_q), .clk(and_1_out), .clr(in_1));  // open: load, D, count, carry
  not not_1 (not_1_out, out_3);
  and and_2 (out_3, counter_1_q[4], ~counter_1_q[3], ~counter_1_q[2], ~counter_1_q[1], ~counter_1_q[0]);  // AND_Gate
endmodule

module jogo (
  input  in_1,
  input  in_2,
  input  in_3,
  input  in_4,
  input  in_5,
  input  in_6,
  input  in_7,
  output out_8,
  output out_9
);

  wire and_1_out, and_2_out, and_3_out, and_4_out, and_5_out, and_6_out, and_7_out, j_k_ff_1_q, j_k_ff_2_q,
       j_k_ff_3_q, j_k_ff_4_q, j_k_ff_5_q, j_k_ff_6_q, not_1_out, not_2_out, not_3_out, not_4_out, not_5_out,
       not_6_out, or_1_out, or_2_out;

  J_K_Flip_Flop j_k_ff_1 (.J(in_1), .clk(in_1), .K(in_1), .Q(j_k_ff_1_q), .reset(in_7));  // open: Qn, preset, en
  J_K_Flip_Flop j_k_ff_2 (.J(in_2), .clk(in_2), .K(in_2), .Q(j_k_ff_2_q), .reset(in_7));  // open: Qn, preset, en
  J_K_Flip_Flop j_k_ff_3 (.J(in_3), .clk(in_3), .K(in_3), .Q(j_k_ff_3_q), .reset(in_7));  // open: Qn, preset, en
  J_K_Flip_Flop j_k_ff_4 (.J(in_4), .clk(in_4), .K(in_4), .Q(j_k_ff_4_q), .reset(in_7));  // open: Qn, preset, en
  J_K_Flip_Flop j_k_ff_5 (.J(in_5), .clk(in_5), .K(in_5), .Q(j_k_ff_5_q), .reset(in_7));  // open: Qn, preset, en
  J_K_Flip_Flop j_k_ff_6 (.J(in_6), .clk(in_6), .K(in_6), .Q(j_k_ff_6_q), .reset(in_7));  // open: Qn, preset, en
  not not_1 (not_1_out, j_k_ff_1_q);
  not not_2 (not_2_out, j_k_ff_3_q);
  not not_3 (not_3_out, j_k_ff_2_q);
  not not_4 (not_4_out, j_k_ff_2_q);
  not not_5 (not_5_out, j_k_ff_1_q);
  not not_6 (not_6_out, j_k_ff_3_q);
  and and_1 (and_1_out, not_1_out, j_k_ff_6_q);
  and and_2 (and_2_out, not_2_out, j_k_ff_5_q);
  and and_3 (and_3_out, not_3_out, j_k_ff_4_q);
  and and_4 (and_4_out, not_4_out, j_k_ff_6_q);
  and and_5 (and_5_out, not_5_out, j_k_ff_5_q);
  and and_6 (and_6_out, not_6_out, j_k_ff_4_q);
  or or_1 (or_1_out, and_1_out, and_2_out, and_3_out);
  or or_2 (or_2_out, and_4_out, and_5_out, and_6_out);
  and and_7 (and_7_out, ~j_k_ff_1_q, ~j_k_ff_2_q, ~j_k_ff_3_q);  // AND_Gate
  and and_8 (out_8, ~and_7_out, or_1_out);  // AND_Gate
  and and_9 (out_9, ~and_7_out, or_2_out);  // AND_Gate
endmodule

module contagem (
  input  [6:0] in_1,
  input  in_2,
  input  in_3,
  output [6:0] out_4,
  output out_5
);

  wire and_1_out;
  wire [6:0] counter_1_q;

  contaDe1A7 contade1a7_1 (.in_2(in_3));  // open: in_1, out_3
  Counter #(.width(7), .max('h7f)) counter_1 (
    .Q(counter_1_q), .clk(and_1_out), .clr(in_2));  // open: load, D, count, carry
  and and_1 (and_1_out, in_3, ~in_2);  // AND_Gate
  Adder #(.width(7)) adder_1 (.a(counter_1_q), .b(in_1), .out(out_4));  // open: cin, cout

  assign out_5 = in_2;
endmodule
