// Logisim project paridade.circ as structural Verilog: 2 circuits, main circuit Paridade
module Paridade (
  input  A,
  input  B,
  input  C,
  input  D,
  output S
);

  wire and_1_out, and_2_out, and_3_out, and_4_out, and_5_out, and_6_out, and_7_out, not_1_out, not_2_out,
       not_3_out, not_4_out, not_5_out, not_6_out, not_7_out, not_8_out, not_9_out, not_10_out, not_11_out,
       not_12_out, not_13_out, not_14_out, not_15_out;

  not not_1 (not_1_out, A);
  not not_2 (not_2_out, B);
  not not_3 (not_3_out, C);
  not not_4 (not_4_out, A);
  not not_5 (not_5_out, B);
  not not_6 (not_6_out, D);
  not not_7 (not_7_out, A);
  not not_8 (not_8_out, C);
  not not_9 (not_9_out, D);
  not not_10 (not_10_out, B);
  not not_11 (not_11_out, C);
  not not_12 (not_12_out, D);
  not not_13 (not_13_out, B);
  not not_14 (not_14_out, C);
  not not_15 (not_15_out, D);
  and and_1 (and_1_out, not_1_out, not_2_out, not_3_out, D);
  and and_2 (and_2_out, not_4_out, not_5_out, C, not_6_out);
  and and_3 (and_3_out, not_7_out, B, not_8_out, not_9_out);
  and and_4 (and_4_out, A, not_10_out, not_11_out, not_12_out);
  and and_5 (and_5_out, A, not_13_out, C, D);
  and and_6 (and_6_out, A, B, not_14_out, D);
  and and_7 (and_7_out, A, B, C, not_15_out);
  or or_1 (S, and_1_out, and_2_out, and_3_out, and_4_out, and_5_out, and_6_out, and_7_out);
endmodule

module Multiplicador (
  input  A,
  input  B,
  input  C,
  input  D,
  output S1,
  output S2,
  output S3,
  output S4
);

  wire and_2_out, and_3_out, and_4_out, and_5_out, and_6_out, and_7_out, not_1_out, not_2_out, not_3_out,
       not_4_out, not_5_out, not_6_out;

  and and_1 (S1, A, B, C, D);
  and and_2 (and_2_out, A, not_1_out, C);
  not not_1 (not_1_out, B);
  and and_3 (and_3_out, A, C, not_2_out);
  not not_2 (not_2_out, D);
  not not_3 (not_3_out, A);
  and and_4 (and_4_out, not_3_out, B, C);
  and and_5 (and_5_out, B, C, not_4_out);
  not not_4 (not_4_out, D);
  and and_6 (and_6_out, A, not_5_out, D);
  not not_5 (not_5_out, B);
  not not_6 (not_6_out, C);
  and and_7 (and_7_out, A, not_6_out, D);
  and and_8 (S4, B, D);
  or or_1 (S2, and_2_out, and_3_out);
  or or_2 (S3, and_4_out, and_5_out, and_6_out, and_7_out);
endmodule
