// Logisim project produto.circ as structural Verilog: 1 circuit, main circuit main
module main (
  input  a,
  input  b,
  input  c,
  input  d,
  output s0,
  output s1,
  output s2,
  output s3
);

  wire and_2_out, and_3_out, and_4_out, and_5_out, and_6_out, and_7_out, not_1_out, not_2_out, not_3_out,
       not_4_out, not_5_out, not_6_out;

  and and_1 (s0, a, b, c, d);
  and and_2 (and_2_out, a, not_1_out, c);
  not not_1 (not_1_out, b);
  and and_3 (and_3_out, a, c, not_2_out);
  not not_2 (not_2_out, d);
  not not_3 (not_3_out, a);
  and and_4 (and_4_out, not_3_out, b, c);
  and and_5 (and_5_out, b, c, not_4_out);
  not not_4 (not_4_out, d);
  and and_6 (and_6_out, a, not_5_out, d);
  not not_5 (not_5_out, b);
  not not_6 (not_6_out, c);
  and and_7 (and_7_out, a, not_6_out, d);
  and and_8 (s3, b, d);
  or or_1 (s1, and_2_out, and_3_out);
  or or_2 (s2, and_4_out, and_5_out, and_6_out, and_7_out);
endmodule
