// Logisim project Laboratório 3 - Circuito 1.circ as structural Verilog: 1 circuit, main circuit main
module main (
  input  f,
  input  i,
  input  p,
  output s
);

  wire and_1_out, and_2_out, not_1_out;

  not not_1 (not_1_out, i);
  and and_1 (and_1_out, i, p);
  and and_2 (and_2_out, f, not_1_out);
  or or_1 (s, and_1_out, and_2_out);
endmodule
