// Logisim project Laboratório 3 - Circuito 2.circ as structural Verilog
module \Laboratório_3___Circuito_2  (
  input  e,
  input  s,
  output a,
  output b
);

  wire and_1_out, and_2_out, and_3_out, and_4_out, not_1_out, not_2_out, not_3_out, not_4_out;

  not not_1 (not_1_out, e);
  not not_2 (not_2_out, s);
  not not_3 (not_3_out, e);
  not not_4 (not_4_out, s);
  and and_1 (and_1_out, not_1_out, s);
  and and_2 (and_2_out, e, not_2_out);
  and and_3 (and_3_out, not_3_out, not_4_out);
  and and_4 (and_4_out, e, s);
  or or_1 (a, and_1_out, and_2_out);
  or or_2 (b, and_3_out, and_4_out);
endmodule
