// Logisim project counter.circ as structural Verilog: 1 circuit, main circuit c_assincrono
module c_assincrono (
  input  in_1
);

  wire clock_1_out;
  wire [3:0] j_k_ff_1_q;

  Clock clock_1 (.out(clock_1_out));
  Hex_Digit_Display hex_digit_display_1 (.value(j_k_ff_1_q));  // open: dp
  J_K_Flip_Flop #(.trigger("falling")) j_k_ff_1 (
    .J(in_1), .clk(clock_1_out), .K(in_1), .Q(j_k_ff_1_q[0]));  // open: Qn, preset, en, reset
  J_K_Flip_Flop #(.trigger("falling")) j_k_ff_2 (
    .J(in_1), .clk(j_k_ff_1_q[0]), .K(in_1), .Q(j_k_ff_1_q[1]));  // open: Qn, preset, en, reset
  J_K_Flip_Flop #(.trigger("falling")) j_k_ff_3 (
    .J(in_1), .clk(j_k_ff_1_q[1]), .K(in_1), .Q(j_k_ff_1_q[2]));  // open: Qn, preset, en, reset
  J_K_Flip_Flop #(.trigger("falling")) j_k_ff_4 (
    .J(in_1), .clk(j_k_ff_1_q[2]), .K(in_1), .Q(j_k_ff_1_q[3]));  // open: Qn, preset, en, reset

  // Notes on the sheet:
  //   Clock
endmodule
