// Logisim project sequence.circ as structural Verilog: 1 circuit, main circuit main
module main (
  input  in_1,
  input  in_2,
  input  in_3,
  input  in_4,
  input  in_5,
  input  in_6
);

  wire d_ff_1_q, d_ff_2_q, d_ff_3_q, d_ff_4_q, d_ff_5_q;

  D_Flip_Flop d_ff_1 (.clk(in_5), .D(in_5), .Q(d_ff_1_q), .reset(in_6));  // open: Qn, preset, en
  D_Flip_Flop d_ff_2 (.clk(in_4), .D(d_ff_1_q), .Q(d_ff_2_q), .reset(in_6));  // open: Qn, preset, en
  D_Flip_Flop d_ff_3 (.clk(in_3), .D(d_ff_2_q), .Q(d_ff_3_q), .reset(in_6));  // open: Qn, preset, en
  D_Flip_Flop d_ff_4 (.clk(in_2), .D(d_ff_3_q), .Q(d_ff_4_q), .reset(in_6));  // open: Qn, preset, en
  D_Flip_Flop d_ff_5 (.clk(in_1), .D(d_ff_4_q), .Q(d_ff_5_q), .reset(in_6));  // open: Qn, preset, en
  LED led_1 (.in(d_ff_5_q));
endmodule
