// Logisim project Circuito 1.circ as structural Verilog: 1 circuit, main circuit main
module main (
  input  in_1,
  input  in_2,
  input  in_3,
  input  in_4,
  input  in_5,
  input  in_6,
  input  in_7
);

  wire and_1_out, and_2_out, and_3_out, and_4_out, clock_1_out, comparator_1_eq;
  wire [5:0] j_k_ff_6_q;

  J_K_Flip_Flop j_k_ff_1 (
    .J(in_5), .clk(clock_1_out), .K(in_5), .Q(j_k_ff_6_q[5]), .reset(comparator_1_eq));  // open: Qn, preset, en
  J_K_Flip_Flop j_k_ff_2 (
    .J(j_k_ff_6_q[5]), .clk(clock_1_out), .K(j_k_ff_6_q[5]), .Q(j_k_ff_6_q[4]), .reset(comparator_1_eq));  // open: Qn, preset, en
  and and_1 (and_1_out, j_k_ff_6_q[5], j_k_ff_6_q[4]);
  J_K_Flip_Flop j_k_ff_3 (
    .J(and_1_out), .clk(clock_1_out), .K(and_1_out), .Q(j_k_ff_6_q[3]), .reset(comparator_1_eq));  // open: Qn, preset, en
  and and_2 (and_2_out, and_1_out, j_k_ff_6_q[3]);
  and and_3 (and_3_out, and_2_out, j_k_ff_6_q[2]);
  J_K_Flip_Flop j_k_ff_4 (
    .J(and_2_out), .clk(clock_1_out), .K(and_2_out), .Q(j_k_ff_6_q[2]), .reset(comparator_1_eq));  // open: Qn, preset, en
  J_K_Flip_Flop j_k_ff_5 (
    .J(and_3_out), .clk(clock_1_out), .K(and_3_out), .Q(j_k_ff_6_q[1]), .reset(comparator_1_eq));  // open: Qn, preset, en
  and and_4 (and_4_out, and_3_out, j_k_ff_6_q[1]);
  J_K_Flip_Flop j_k_ff_6 (
    .J(and_4_out), .clk(clock_1_out), .K(and_4_out), .Q(j_k_ff_6_q[0]), .reset(comparator_1_eq));  // open: Qn, preset, en
  Clock clock_1 (.out(clock_1_out));
  Comparator #(.width(6)) comparator_1 (
    .a(j_k_ff_6_q), .b({in_7, in_6, in_4, in_3, in_2, in_1}), .eq(comparator_1_eq));  // open: gt, lt
endmodule
