// Logisim project contador.circ as structural Verilog: 3 circuits, main circuit main
module main (
);

  wire [3:0] contador_1_out_4;

  contador contador_1 (
    .out_1(contador_1_out_4[3]), .out_2(contador_1_out_4[2]), .out_3(contador_1_out_4[1]),
    .out_4(contador_1_out_4[0]));
  Hex_Digit_Display hex_digit_display_1 (.value(contador_1_out_4));  // open: dp
endmodule

module contador (
  output out_1,
  output out_2,
  output out_3,
  output out_4
);

  wire button_1_out, clock_1_out, logica_1_ja, logica_1_jb, logica_1_jc, logica_1_jd, logica_1_ka,
       logica_1_kb, logica_1_kc, logica_1_kd;

  Clock clock_1 (.out(clock_1_out));
  Button button_1 (.out(button_1_out));
  J_K_Flip_Flop A (
    .J(logica_1_ja), .clk(clock_1_out), .K(logica_1_ka), .Q(out_1), .reset(button_1_out));  // open: Qn, preset, en
  logica logica_1 (
    .a(out_1), .b(out_2), .c(out_3), .d(out_4), .ja(logica_1_ja), .ka(logica_1_ka), .jb(logica_1_jb),
    .kb(logica_1_kb), .jc(logica_1_jc), .kc(logica_1_kc), .jd(logica_1_jd), .kd(logica_1_kd));
  J_K_Flip_Flop B (
    .J(logica_1_jb), .clk(clock_1_out), .K(logica_1_kb), .Q(out_2), .reset(button_1_out));  // open: Qn, preset, en
  J_K_Flip_Flop C (
    .J(logica_1_jc), .clk(clock_1_out), .K(logica_1_kc), .Q(out_3), .reset(button_1_out));  // open: Qn, preset, en
  J_K_Flip_Flop D (
    .J(logica_1_jd), .clk(clock_1_out), .K(logica_1_kd), .Q(out_4), .reset(button_1_out));  // open: Qn, preset, en
endmodule

module logica (
  input  a,
  input  b,
  input  c,
  input  d,
  output ja,
  output ka,
  output jb,
  output kb,
  output jc,
  output kc,
  output jd,
  output kd
);

  wire and_1_out, and_2_out, and_3_out, and_4_out, and_5_out, and_6_out, and_7_out, and_8_out, and_9_out,
       and_10_out, and_11_out, and_12_out, and_13_out, and_14_out, and_15_out, and_16_out, and_17_out,
       and_18_out, not_1_out, not_2_out, not_3_out, not_4_out, not_5_out, not_6_out, not_7_out, not_8_out,
       not_9_out, not_10_out, not_11_out, not_13_out, not_14_out, not_15_out, not_16_out, not_17_out,
       not_18_out, not_19_out, not_20_out, not_21_out, not_22_out;

  not not_1 (not_1_out, a);
  and and_1 (and_1_out, not_1_out, b, c);
  and and_2 (and_2_out, a, not_2_out);
  not not_2 (not_2_out, b);
  and and_3 (and_3_out, a, not_3_out);
  not not_3 (not_3_out, c);
  not not_4 (not_4_out, a);
  and and_4 (and_4_out, not_4_out, not_5_out);
  not not_5 (not_5_out, b);
  not not_6 (not_6_out, a);
  and and_5 (and_5_out, not_6_out, not_7_out);
  not not_7 (not_7_out, c);
  and and_6 (and_6_out, a, b, c);
  not not_8 (not_8_out, b);
  and and_7 (and_7_out, not_8_out, c);
  and and_8 (and_8_out, b, not_9_out);
  not not_9 (not_9_out, c);
  not not_10 (not_10_out, b);
  and and_9 (and_9_out, not_10_out, not_11_out);
  not not_11 (not_11_out, c);
  and and_10 (and_10_out, b, c);
  not not_12 (jc, c);
  not not_13 (not_13_out, a);
  not not_14 (not_14_out, b);
  not not_15 (not_15_out, c);
  not not_16 (not_16_out, d);
  not not_17 (not_17_out, a);
  and and_11 (and_11_out, not_17_out, not_18_out);
  not not_18 (not_18_out, d);
  not not_19 (not_19_out, b);
  and and_12 (and_12_out, not_19_out, not_20_out);
  not not_20 (not_20_out, d);
  not not_21 (not_21_out, c);
  and and_13 (and_13_out, not_21_out, not_22_out);
  not not_22 (not_22_out, d);
  and and_14 (and_14_out, a, b, c, d);
  or or_1 (ja, and_1_out, and_2_out, and_3_out);
  or or_2 (ka, and_4_out, and_5_out, and_6_out);
  or or_3 (jb, and_7_out, and_8_out);
  or or_4 (kb, and_9_out, and_10_out);
  and and_15 (and_15_out, not_13_out, d);
  and and_16 (and_16_out, not_14_out, d);
  and and_17 (and_17_out, not_15_out, d);
  and and_18 (and_18_out, a, b, c, not_16_out);
  or or_5 (kd, and_11_out, and_12_out, and_13_out, and_14_out);
  or or_6 (jd, and_15_out, and_16_out, and_17_out, and_18_out);

  assign kc = c;
endmodule
