// Logisim project circuito.circ as structural Verilog: 1 circuit, main circuit main
module main (
  input  in_1,
  input  in_2,
  input  in_3,
  input  in_4,
  input  in_5,
  input  in_6,
  input  in_7,
  input  in_8
);

  wire clock_1_out, d_ff_1_q, d_ff_2_q, d_ff_3_q, d_ff_4_q, d_ff_5_q, d_ff_6_q, d_ff_7_q, d_ff_8_q,
       demultiplexer_1_out0, demultiplexer_1_out1, demultiplexer_1_out2, demultiplexer_1_out3,
       demultiplexer_1_out4, demultiplexer_1_out5, demultiplexer_1_out6, demultiplexer_1_out7,
       multiplexer_1_out;
  wire [2:0] counter_1_q, counter_2_q;

  Clock clock_1 (.out(clock_1_out));
  Counter #(.width(3), .max('h7)) counter_1 (.Q(counter_1_q), .clk(clock_1_out));  // open: load, D, count, carry, clr
  Multiplexer #(.select(3), .enable("false")) multiplexer_1 (
    .in0(in_1), .in1(in_2), .in2(in_3), .in3(in_4), .in4(in_5), .in5(in_6), .in6(in_7), .in7(in_8),
    .out(multiplexer_1_out), .sel(counter_1_q));
  Demultiplexer #(.select(3), .tristate("true"), .enable("false")) demultiplexer_1 (
    .out0(demultiplexer_1_out0), .out1(demultiplexer_1_out1), .out2(demultiplexer_1_out2),
    .out3(demultiplexer_1_out3), .out4(demultiplexer_1_out4), .out5(demultiplexer_1_out5),
    .out6(demultiplexer_1_out6), .out7(demultiplexer_1_out7), .in(multiplexer_1_out), .sel(counter_2_q));
  Counter #(.width(3), .max('h7)) counter_2 (
    .D(counter_1_q), .Q(counter_2_q), .clk(clock_1_out));  // open: load, count, carry, clr
  D_Flip_Flop d_ff_1 (.Q(d_ff_1_q), .preset(demultiplexer_1_out0));  // open: clk, D, Qn, en, reset
  D_Flip_Flop d_ff_2 (.Q(d_ff_2_q), .preset(demultiplexer_1_out1));  // open: clk, D, Qn, en, reset
  D_Flip_Flop d_ff_3 (.Q(d_ff_3_q), .preset(demultiplexer_1_out2));  // open: clk, D, Qn, en, reset
  D_Flip_Flop d_ff_4 (.Q(d_ff_4_q), .preset(demultiplexer_1_out3));  // open: clk, D, Qn, en, reset
  D_Flip_Flop d_ff_5 (.Q(d_ff_5_q), .preset(demultiplexer_1_out4));  // open: clk, D, Qn, en, reset
  D_Flip_Flop d_ff_6 (.Q(d_ff_6_q), .preset(demultiplexer_1_out5));  // open: clk, D, Qn, en, reset
  LED led_1 (.in(d_ff_1_q));
  LED led_2 (.in(d_ff_2_q));
  LED led_3 (.in(d_ff_3_q));
  LED led_4 (.in(d_ff_4_q));
  LED led_5 (.in(d_ff_5_q));
  LED led_6 (.in(d_ff_6_q));
  LED led_7 (.in(d_ff_7_q));
  D_Flip_Flop d_ff_7 (.Q(d_ff_7_q), .preset(demultiplexer_1_out6));  // open: clk, D, Qn, en, reset
  LED led_8 (.in(d_ff_8_q));
  D_Flip_Flop d_ff_8 (.Q(d_ff_8_q), .preset(demultiplexer_1_out7));  // open: clk, D, Qn, en, reset
endmodule
